// Logisim project branch_comp.circ as structural Verilog: 1 circuit, main circuit branch_comp
module branch_comp (
  input  [31:0] rs1,
  input  [31:0] rs2,
  input  BrUn,
  output BrEq,
  output BrLt
);

  wire comparator_2_eq, comparator_3_eq, comparator_3_lt, ge, multiplexer_2_out, multiplexer_3_out,
       multiplexer_4_out, signEq, signLt, unsignEq, unsignLt1, unsignLt2;
  wire [31:0] bit_extender_1_out, bit_extender_2_out;

  Multiplexer #(.enable("false")) multiplexer_1 (.in0(signEq), .in1(unsignEq), .out(BrEq), .sel(BrUn));
  Comparator #(.width(32)) comparator_1 (.a(rs1), .b(rs2), .eq(signEq), .lt(signLt));  // open: gt
  Multiplexer #(.enable("false")) multiplexer_2 (.in0(1'b0), .in1(1'b1), .out(multiplexer_2_out), .sel(unsignLt1));
  assign bit_extender_1_out = {{1{rs1[30]}}, rs1[30:0]};  // Bit_Extender bit_extender_1
  assign bit_extender_2_out = {{1{rs2[30]}}, rs2[30:0]};  // Bit_Extender bit_extender_2
  Multiplexer #(.enable("false")) multiplexer_3 (
    .in0(multiplexer_2_out), .in1(1'b1), .out(multiplexer_3_out), .sel(unsignLt2));
  Comparator #(.width(1)) comparator_2 (.a(rs2[31]), .b(rs1[31]), .gt(ge), .eq(comparator_2_eq), .lt(unsignLt1));
  Comparator #(.width(32)) comparator_3 (
    .a(bit_extender_1_out), .b(bit_extender_2_out), .eq(comparator_3_eq), .lt(comparator_3_lt));  // open: gt
  Multiplexer #(.enable("false")) multiplexer_4 (
    .in0(multiplexer_3_out), .in1(1'b0), .out(multiplexer_4_out), .sel(ge));
  Multiplexer #(.enable("false")) multiplexer_5 (.in0(signLt), .in1(multiplexer_4_out), .out(BrLt), .sel(BrUn));
  and and_1 (unsignEq, comparator_2_eq, comparator_3_eq);
  and and_2 (unsignLt2, comparator_2_eq, comparator_3_lt);

  // Notes on the sheet:
  //   INPUTS to your circuit
  //   DON'T CHANGE THE LOCATIONS OF THE INPUTS AND OUTPUTS!
  //   OUTPUT from your circuit
endmodule
