// Logisim project control_logic.circ as structural Verilog: 1 circuit, main circuit control_logic
module control_logic (
  input  [31:0] inst,
  input  BrEq,
  input  BrLt,
  output PCSel,
  output RegWEn,
  output [2:0] ImmSel,
  output BrUn,
  output ASel,
  output BSel,
  output [3:0] ALUSel,
  output MemRW,
  output [1:0] WBSel,
  output CSRSel,
  output CSRWen
);

  wire add, addi, and1, and_1_out, and_2_out, and_3_out, and_4_out, and_5_out, and_6_out, and_7_out,
       and_8_out, and_9_out, and_10_out, and_11_out, and_12_out, and_13_out, and_14_out, and_15_out,
       and_16_out, and_17_out, and_18_out, and_19_out, and_20_out, and_21_out, and_22_out, and_23_out,
       and_24_out, and_25_out, and_26_out, and_27_out, and_28_out, and_29_out, and_30_out, and_31_out,
       and_32_out, andi, auipc, beq, bge, bgeu, blt, bltu, bne, comparator_11_eq, comparator_12_eq,
       comparator_13_eq, comparator_14_eq, comparator_15_eq, comparator_16_eq, comparator_17_eq,
       comparator_18_eq, comparator_19_eq, comparator_20_eq, comparator_21_eq, comparator_22_eq,
       comparator_23_eq, comparator_24_eq, comparator_25_eq, comparator_26_eq, comparator_27_eq,
       comparator_28_eq, comparator_29_eq, comparator_30_eq, comparator_31_eq, comparator_32_eq,
       comparator_33_eq, comparator_34_eq, comparator_35_eq, comparator_36_eq, comparator_37_eq,
       comparator_38_eq, comparator_39_eq, comparator_40_eq, comparator_41_eq, comparator_42_eq,
       comparator_43_eq, comparator_44_eq, comparator_45_eq, comparator_46_eq, comparator_47_eq,
       comparator_48_eq, comparator_49_eq, comparator_50_eq, comparator_51_eq, comparator_52_eq,
       comparator_53_eq, comparator_54_eq, csrw, I_03, I_13, I_67, I_73, jair, jal, lb, lh, lui, lw, mul,
       mulh, mulhu, nor_2_out, not_2_out, not_3_out, or1, or_1_out, or_4_out, or_5_out, or_6_out, or_10_out,
       or_11_out, or_12_out, or_13_out, ori, R, SB, sb_t, sh, sll1, slli, slt, slti, sra1, srai, srl1, srli,
       sub, sw, xor1, xori;
  wire [1:0] multiplexer_1_out, multiplexer_2_out, multiplexer_13_out;
  wire [2:0] I_03func3, I_13func3, I_67func3, I_73func3, multiplexer_3_out, multiplexer_4_out,
       multiplexer_5_out, multiplexer_6_out, multiplexer_7_out, multiplexer_8_out, multiplexer_9_out,
       multiplexer_10_out, multiplexer_11_out, multiplexer_12_out, Rfunc3, SBfunc3, Sfunc3;
  wire [3:0] multiplexer_22_out, multiplexer_23_out, multiplexer_24_out, multiplexer_25_out,
       multiplexer_26_out, multiplexer_27_out, multiplexer_28_out, multiplexer_29_out, multiplexer_30_out,
       multiplexer_31_out, multiplexer_32_out, multiplexer_33_out, multiplexer_34_out, multiplexer_35_out,
       multiplexer_36_out, multiplexer_37_out, multiplexer_38_out, multiplexer_39_out;
  wire [4:0] rd, rs1, rs2;
  wire [6:0] func7;

  Comparator #(.width(7)) comparator_1 (.a(7'b0110011), .b(inst[6:0]), .eq(R));  // open: gt, lt
  Comparator #(.width(7)) comparator_2 (.a(7'b0000011), .b(inst[6:0]), .eq(I_03));  // open: gt, lt
  Comparator #(.width(7)) comparator_3 (.a(7'b0010011), .b(inst[6:0]), .eq(I_13));  // open: gt, lt
  Comparator #(.width(7)) comparator_4 (.a(7'b0100011), .b(inst[6:0]), .eq(MemRW));  // open: gt, lt
  Comparator #(.width(7)) comparator_5 (.a(7'b1100011), .b(inst[6:0]), .eq(SB));  // open: gt, lt
  Comparator #(.width(7)) comparator_6 (.a(7'b0010111), .b(inst[6:0]), .eq(auipc));  // open: gt, lt
  Comparator #(.width(7)) comparator_7 (.a(7'b0110111), .b(inst[6:0]), .eq(lui));  // open: gt, lt
  Comparator #(.width(7)) comparator_8 (.a(7'b1101111), .b(inst[6:0]), .eq(jal));  // open: gt, lt
  Comparator #(.width(7)) comparator_9 (.a(7'b1100111), .b(inst[6:0]), .eq(I_67));  // open: gt, lt
  Comparator #(.width(7)) comparator_10 (.a(7'b1110011), .b(inst[6:0]), .eq(I_73));  // open: gt, lt
  or or_1 (or_1_out, R, lui, auipc, I_13);
  nor nor_1 (RegWEn, MemRW, SB);
  or or_2 (BrUn, bltu, bgeu);
  not not_1 (BSel, R);
  Multiplexer #(.enable("false"), .width(2)) multiplexer_1 (
    .in0(2'b00), .in1(2'b01), .out(multiplexer_1_out), .sel(or_1_out));
  and and_1 (and_1_out, BrEq, beq);
  assign WBSel = multiplexer_1_out | multiplexer_2_out | multiplexer_13_out;  // OR_Gate or_3, 2 bits wide
  Multiplexer #(.enable("false"), .width(2)) multiplexer_2 (
    .in0(2'b00), .in1(2'b10), .out(multiplexer_2_out), .sel(I_03));
  or or_4 (or_4_out, and_1_out, and_2_out, and_3_out, and_4_out);
  and and_2 (and_2_out, BrLt, or_5_out);
  or or_5 (or_5_out, bltu, blt);
  Multiplexer #(.enable("false"), .width(3)) multiplexer_3 (
    .in0(3'b000), .in1(3'b000), .out(multiplexer_3_out), .sel(R));
  Multiplexer #(.enable("false"), .width(3)) multiplexer_4 (
    .in0(3'b000), .in1(3'b001), .out(multiplexer_4_out), .sel(I_03));
  Multiplexer #(.enable("false"), .width(3)) multiplexer_5 (
    .in0(3'b000), .in1(3'b001), .out(multiplexer_5_out), .sel(I_13));
  Multiplexer #(.enable("false"), .width(3)) multiplexer_6 (
    .in0(3'b000), .in1(3'b010), .out(multiplexer_6_out), .sel(MemRW));
  Multiplexer #(.enable("false"), .width(3)) multiplexer_7 (
    .in0(3'b000), .in1(3'b011), .out(multiplexer_7_out), .sel(SB));
  Multiplexer #(.enable("false"), .width(3)) multiplexer_8 (
    .in0(3'b000), .in1(3'b100), .out(multiplexer_8_out), .sel(auipc));
  Multiplexer #(.enable("false"), .width(3)) multiplexer_9 (
    .in0(3'b000), .in1(3'b100), .out(multiplexer_9_out), .sel(lui));
  Multiplexer #(.enable("false"), .width(3)) multiplexer_10 (
    .in0(3'b000), .in1(3'b101), .out(multiplexer_10_out), .sel(jal));
  Multiplexer #(.enable("false"), .width(3)) multiplexer_11 (
    .in0(3'b000), .in1(3'b001), .out(multiplexer_11_out), .sel(I_67));
  Multiplexer #(.enable("false"), .width(3)) multiplexer_12 (
    .in0(3'b000), .in1(3'b001), .out(multiplexer_12_out), .sel(I_73));
  Multiplexer #(.enable("false"), .width(2)) multiplexer_13 (
    .in0(2'b00), .in1(2'b11), .out(multiplexer_13_out), .sel(or_6_out));
  or or_6 (or_6_out, jal, I_67);
  or or_7 (PCSel, or_4_out, I_67, jal);
  and and_3 (and_3_out, not_2_out, bne);
  not not_2 (not_2_out, BrEq);
  and and_4 (and_4_out, not_3_out, or_10_out);
  not not_3 (not_3_out, and_5_out);
  and and_5 (and_5_out, BrLt, BrEq);
  assign ImmSel = multiplexer_3_out | multiplexer_4_out | multiplexer_5_out | multiplexer_6_out | multiplexer_7_out | multiplexer_8_out | multiplexer_9_out | multiplexer_10_out | multiplexer_11_out | multiplexer_12_out;  // OR_Gate or_8, 3 bits wide
  or or_9 (ASel, I_13, I_03, MemRW, I_67, R, auipc, lui);
  or or_10 (or_10_out, bge, bgeu);
  Multiplexer #(.enable("false"), .width(3)) multiplexer_14 (.in0(3'b000), .in1(inst[14:12]), .out(Rfunc3), .sel(R));
  Multiplexer #(.enable("false"), .width(3)) multiplexer_15 (
    .in0(3'b000), .in1(inst[14:12]), .out(I_03func3), .sel(I_03));
  Multiplexer #(.enable("false"), .width(3)) multiplexer_16 (
    .in0(3'b000), .in1(inst[14:12]), .out(I_13func3), .sel(I_13));
  Multiplexer #(.enable("false"), .width(3)) multiplexer_17 (
    .in0(3'b000), .in1(inst[14:12]), .out(I_67func3), .sel(I_67));
  Multiplexer #(.enable("false"), .width(3)) multiplexer_18 (
    .in0(3'b000), .in1(inst[14:12]), .out(I_73func3), .sel(I_73));
  Multiplexer #(.enable("false"), .width(3)) multiplexer_19 (
    .in0(3'b000), .in1(inst[14:12]), .out(Sfunc3), .sel(MemRW));
  Multiplexer #(.enable("false"), .width(3)) multiplexer_20 (.in0(3'b000), .in1(inst[14:12]), .out(SBfunc3), .sel(SB));
  Multiplexer #(.enable("false"), .width(7)) multiplexer_21 (.in0({7{1'b0}}), .in1(inst[31:25]), .out(func7), .sel(R));
  Multiplexer #(.enable("false"), .width(4)) multiplexer_22 (
    .in0(4'b0000), .in1(4'b0001), .out(multiplexer_22_out), .sel(and_6_out));
  and and_6 (and_6_out, and1, R);
  Multiplexer #(.enable("false"), .width(4)) multiplexer_23 (
    .in0(4'b0000), .in1(4'b0001), .out(multiplexer_23_out), .sel(and_7_out));
  and and_7 (and_7_out, andi, I_13);
  Multiplexer #(.enable("false"), .width(4)) multiplexer_24 (
    .in0(4'b0000), .in1(4'b0010), .out(multiplexer_24_out), .sel(and_8_out));
  and and_8 (and_8_out, or1, R);
  Multiplexer #(.enable("false"), .width(4)) multiplexer_25 (
    .in0(4'b0000), .in1(4'b0010), .out(multiplexer_25_out), .sel(and_9_out));
  and and_9 (and_9_out, ori, I_13);
  Multiplexer #(.enable("false"), .width(4)) multiplexer_26 (
    .in0(4'b0000), .in1(4'b0011), .out(multiplexer_26_out), .sel(and_10_out));
  and and_10 (and_10_out, xor1, R);
  Multiplexer #(.enable("false"), .width(4)) multiplexer_27 (
    .in0(4'b0000), .in1(4'b0011), .out(multiplexer_27_out), .sel(and_11_out));
  and and_11 (and_11_out, xori, I_13);
  Multiplexer #(.enable("false"), .width(4)) multiplexer_28 (
    .in0(4'b0000), .in1(4'b0100), .out(multiplexer_28_out), .sel(and_12_out));
  and and_12 (and_12_out, srl1, R);
  Multiplexer #(.enable("false"), .width(4)) multiplexer_29 (
    .in0(4'b0000), .in1(4'b0100), .out(multiplexer_29_out), .sel(and_13_out));
  and and_13 (and_13_out, srli, I_13);
  Multiplexer #(.enable("false"), .width(4)) multiplexer_30 (
    .in0(4'b0000), .in1(4'b0101), .out(multiplexer_30_out), .sel(and_14_out));
  and and_14 (and_14_out, sra1, R);
  Multiplexer #(.enable("false"), .width(4)) multiplexer_31 (
    .in0(4'b0000), .in1(4'b0101), .out(multiplexer_31_out), .sel(and_15_out));
  and and_15 (and_15_out, srai, I_13);
  Multiplexer #(.enable("false"), .width(4)) multiplexer_32 (
    .in0(4'b0000), .in1(4'b0110), .out(multiplexer_32_out), .sel(and_16_out));
  and and_16 (and_16_out, sll1, R);
  Multiplexer #(.enable("false"), .width(4)) multiplexer_33 (
    .in0(4'b0000), .in1(4'b0110), .out(multiplexer_33_out), .sel(and_17_out));
  and and_17 (and_17_out, slli, I_13);
  Multiplexer #(.enable("false"), .width(4)) multiplexer_34 (
    .in0(4'b0000), .in1(4'b0111), .out(multiplexer_34_out), .sel(and_18_out));
  and and_18 (and_18_out, slt, R);
  Multiplexer #(.enable("false"), .width(4)) multiplexer_35 (
    .in0(4'b0000), .in1(4'b0111), .out(multiplexer_35_out), .sel(and_19_out));
  and and_19 (and_19_out, slti, I_13);
  Multiplexer #(.enable("false"), .width(4)) multiplexer_36 (
    .in0(4'b0000), .in1(4'b1010), .out(multiplexer_36_out), .sel(and_20_out));
  and and_20 (and_20_out, mul, R);
  Multiplexer #(.enable("false"), .width(4)) multiplexer_37 (
    .in0(4'b0000), .in1(4'b1011), .out(multiplexer_37_out), .sel(and_21_out));
  and and_21 (and_21_out, mulhu, R);
  Multiplexer #(.enable("false"), .width(4)) multiplexer_38 (
    .in0(4'b0000), .in1(4'b1100), .out(multiplexer_38_out), .sel(and_22_out));
  and and_22 (and_22_out, sub, R);
  Multiplexer #(.enable("false"), .width(4)) multiplexer_39 (
    .in0(4'b0000), .in1(4'b1110), .out(multiplexer_39_out), .sel(and_23_out));
  and and_23 (and_23_out, mulh, R);
  nor nor_2 (nor_2_out, MemRW, SB);
  or or_11 (or_11_out, R, MemRW, SB);
  Multiplexer #(.enable("false"), .width(5)) multiplexer_40 (
    .in0({5{1'b0}}), .in1(inst[11:7]), .out(rd), .sel(nor_2_out));
  Multiplexer #(.enable("false"), .width(5)) multiplexer_41 (
    .in0({5{1'b0}}), .in1(inst[19:15]), .out(rs1), .sel(or_12_out));
  or or_12 (or_12_out, R, MemRW, SB, or_13_out);
  Multiplexer #(.enable("false"), .width(5)) multiplexer_42 (
    .in0({5{1'b0}}), .in1(inst[24:20]), .out(rs2), .sel(or_11_out));
  or or_13 (or_13_out, I_03, I_13, I_67, I_73);
  Comparator #(.width(7)) comparator_11 (.a({7{1'b0}}), .b(func7), .eq(comparator_11_eq));  // open: gt, lt
  Comparator #(.width(3)) comparator_12 (.a(3'b000), .b(Rfunc3), .eq(comparator_12_eq));  // open: gt, lt
  Comparator #(.width(7)) comparator_13 (.a(7'b0000001), .b(func7), .eq(comparator_13_eq));  // open: gt, lt
  Comparator #(.width(3)) comparator_14 (.a(3'b000), .b(Rfunc3), .eq(comparator_14_eq));  // open: gt, lt
  Comparator #(.width(7)) comparator_15 (.a(7'b0100000), .b(func7), .eq(comparator_15_eq));  // open: gt, lt
  Comparator #(.width(3)) comparator_16 (.a(3'b000), .b(Rfunc3), .eq(comparator_16_eq));  // open: gt, lt
  Comparator #(.width(7)) comparator_17 (.a({7{1'b0}}), .b(func7), .eq(comparator_17_eq));  // open: gt, lt
  Comparator #(.width(3)) comparator_18 (.a(3'b001), .b(Rfunc3), .eq(comparator_18_eq));  // open: gt, lt
  Comparator #(.width(7)) comparator_19 (.a(7'b0000001), .b(func7), .eq(comparator_19_eq));  // open: gt, lt
  Comparator #(.width(3)) comparator_20 (.a(3'b001), .b(Rfunc3), .eq(comparator_20_eq));  // open: gt, lt
  Comparator #(.width(3)) comparator_21 (.a(3'b010), .b(Rfunc3), .eq(comparator_21_eq));  // open: gt, lt
  Comparator #(.width(3)) comparator_22 (.a(3'b011), .b(Rfunc3), .eq(comparator_22_eq));  // open: gt, lt
  Comparator #(.width(3)) comparator_23 (.a(3'b100), .b(Rfunc3), .eq(comparator_23_eq));  // open: gt, lt
  Comparator #(.width(7)) comparator_24 (.a({7{1'b0}}), .b(func7), .eq(comparator_24_eq));  // open: gt, lt
  Comparator #(.width(3)) comparator_25 (.a(3'b101), .b(Rfunc3), .eq(comparator_25_eq));  // open: gt, lt
  Comparator #(.width(7)) comparator_26 (.a(7'b0100000), .b(func7), .eq(comparator_26_eq));  // open: gt, lt
  Comparator #(.width(3)) comparator_27 (.a(3'b101), .b(Rfunc3), .eq(comparator_27_eq));  // open: gt, lt
  Comparator #(.width(3)) comparator_28 (.a(3'b110), .b(Rfunc3), .eq(comparator_28_eq));  // open: gt, lt
  Comparator #(.width(3)) comparator_29 (.a(3'b111), .b(Rfunc3), .eq(comparator_29_eq));  // open: gt, lt
  assign ALUSel = multiplexer_22_out | multiplexer_23_out | multiplexer_24_out | multiplexer_25_out | multiplexer_26_out | multiplexer_27_out | multiplexer_28_out | multiplexer_29_out | multiplexer_30_out | multiplexer_31_out | multiplexer_32_out | multiplexer_33_out | multiplexer_34_out | multiplexer_35_out | multiplexer_36_out | multiplexer_37_out | multiplexer_38_out | multiplexer_39_out;  // OR_Gate or_14, 4 bits wide
  and and_24 (and_24_out, comparator_11_eq, comparator_12_eq);
  and and_25 (and_25_out, comparator_13_eq, comparator_14_eq);
  and and_26 (and_26_out, comparator_15_eq, comparator_16_eq);
  and and_27 (and_27_out, comparator_17_eq, comparator_18_eq);
  and and_28 (and_28_out, comparator_19_eq, comparator_20_eq);
  Multiplexer #(.enable("false")) multiplexer_43 (.in0(1'b0), .in1(comparator_21_eq), .out(slt), .sel(R));
  Multiplexer #(.enable("false")) multiplexer_44 (.in0(1'b0), .in1(comparator_22_eq), .out(mulhu), .sel(R));
  Multiplexer #(.enable("false")) multiplexer_45 (.in0(1'b0), .in1(comparator_23_eq), .out(xor1), .sel(R));
  and and_29 (and_29_out, comparator_24_eq, comparator_25_eq);
  and and_30 (and_30_out, comparator_26_eq, comparator_27_eq);
  Multiplexer #(.enable("false")) multiplexer_46 (.in0(1'b0), .in1(comparator_28_eq), .out(or1), .sel(R));
  Multiplexer #(.enable("false")) multiplexer_47 (.in0(1'b0), .in1(comparator_29_eq), .out(and1), .sel(R));
  Multiplexer #(.enable("false")) multiplexer_48 (.in0(1'b0), .in1(and_24_out), .out(add), .sel(R));
  Multiplexer #(.enable("false")) multiplexer_49 (.in0(1'b0), .in1(and_25_out), .out(mul), .sel(R));
  Multiplexer #(.enable("false")) multiplexer_50 (.in0(1'b0), .in1(and_26_out), .out(sub), .sel(R));
  Multiplexer #(.enable("false")) multiplexer_51 (.in0(1'b0), .in1(and_27_out), .out(sll1), .sel(R));
  Multiplexer #(.enable("false")) multiplexer_52 (.in0(1'b0), .in1(and_28_out), .out(mulh), .sel(R));
  Multiplexer #(.enable("false")) multiplexer_53 (.in0(1'b0), .in1(and_29_out), .out(srl1), .sel(R));
  Multiplexer #(.enable("false")) multiplexer_54 (.in0(1'b0), .in1(and_30_out), .out(sra1), .sel(R));
  Comparator #(.width(3)) comparator_30 (.a(3'b000), .b(I_03func3), .eq(comparator_30_eq));  // open: gt, lt
  Comparator #(.width(3)) comparator_31 (.a(3'b001), .b(I_03func3), .eq(comparator_31_eq));  // open: gt, lt
  Comparator #(.width(3)) comparator_32 (.a(3'b010), .b(I_03func3), .eq(comparator_32_eq));  // open: gt, lt
  Comparator #(.width(3)) comparator_33 (.a(3'b000), .b(I_13func3), .eq(comparator_33_eq));  // open: gt, lt
  Comparator #(.width(3)) comparator_34 (.a(3'b001), .b(I_13func3), .eq(comparator_34_eq));  // open: gt, lt
  Comparator #(.width(3)) comparator_35 (.a(3'b010), .b(I_13func3), .eq(comparator_35_eq));  // open: gt, lt
  Comparator #(.width(3)) comparator_36 (.a(3'b100), .b(I_13func3), .eq(comparator_36_eq));  // open: gt, lt
  Comparator #(.width(3)) comparator_37 (.a(3'b101), .b(I_13func3), .eq(comparator_37_eq));  // open: gt, lt
  Comparator #(.width(7)) comparator_38 (.a({7{1'b0}}), .b(inst[31:25]), .eq(comparator_38_eq));  // open: gt, lt
  Comparator #(.width(3)) comparator_39 (.a(3'b101), .b(I_13func3), .eq(comparator_39_eq));  // open: gt, lt
  Comparator #(.width(7)) comparator_40 (.a(7'b0100000), .b(inst[31:25]), .eq(comparator_40_eq));  // open: gt, lt
  Comparator #(.width(3)) comparator_41 (.a(3'b110), .b(I_13func3), .eq(comparator_41_eq));  // open: gt, lt
  Comparator #(.width(3)) comparator_42 (.a(3'b111), .b(I_13func3), .eq(comparator_42_eq));  // open: gt, lt
  Comparator #(.width(3)) comparator_43 (.a(3'b000), .b(I_67func3), .eq(comparator_43_eq));  // open: gt, lt
  Comparator #(.width(3)) comparator_44 (.a(3'b001), .b(I_73func3), .eq(comparator_44_eq));  // open: gt, lt
  Comparator #(.width(3)) comparator_45 (.a(3'b101), .b(I_73func3), .eq(comparator_45_eq));  // open: gt, lt
  or or_15 (CSRWen, csrw, CSRSel);
  Multiplexer #(.enable("false")) multiplexer_55 (.in0(1'b0), .in1(comparator_30_eq), .out(lb), .sel(I_03));
  Multiplexer #(.enable("false")) multiplexer_56 (.in0(1'b0), .in1(comparator_32_eq), .out(lw), .sel(I_03));
  Multiplexer #(.enable("false")) multiplexer_57 (.in0(1'b0), .in1(comparator_34_eq), .out(slli), .sel(I_13));
  Multiplexer #(.enable("false")) multiplexer_58 (.in0(1'b0), .in1(comparator_35_eq), .out(slti), .sel(I_13));
  Multiplexer #(.enable("false")) multiplexer_59 (.in0(1'b0), .in1(comparator_36_eq), .out(xori), .sel(I_13));
  and and_31 (and_31_out, comparator_37_eq, comparator_38_eq);
  and and_32 (and_32_out, comparator_39_eq, comparator_40_eq);
  Multiplexer #(.enable("false")) multiplexer_60 (.in0(1'b0), .in1(comparator_41_eq), .out(ori), .sel(I_13));
  Multiplexer #(.enable("false")) multiplexer_61 (.in0(1'b0), .in1(comparator_43_eq), .out(jair), .sel(I_67));
  Multiplexer #(.enable("false")) multiplexer_62 (.in0(1'b0), .in1(comparator_44_eq), .out(csrw), .sel(I_73));
  Multiplexer #(.enable("false")) multiplexer_63 (.in0(1'b0), .in1(comparator_45_eq), .out(CSRSel), .sel(I_73));
  Multiplexer #(.enable("false")) multiplexer_64 (.in0(1'b0), .in1(comparator_31_eq), .out(lh), .sel(I_03));
  Multiplexer #(.enable("false")) multiplexer_65 (.in0(1'b0), .in1(comparator_33_eq), .out(addi), .sel(I_13));
  Multiplexer #(.enable("false")) multiplexer_66 (.in0(1'b0), .in1(and_31_out), .out(srli), .sel(I_13));
  Multiplexer #(.enable("false")) multiplexer_67 (.in0(1'b0), .in1(and_32_out), .out(srai), .sel(I_13));
  Multiplexer #(.enable("false")) multiplexer_68 (.in0(1'b0), .in1(comparator_42_eq), .out(andi), .sel(I_13));
  Comparator #(.width(3)) comparator_46 (.a(3'b000), .b(Sfunc3), .eq(comparator_46_eq));  // open: gt, lt
  Comparator #(.width(3)) comparator_47 (.a(3'b001), .b(Sfunc3), .eq(comparator_47_eq));  // open: gt, lt
  Comparator #(.width(3)) comparator_48 (.a(3'b010), .b(Sfunc3), .eq(comparator_48_eq));  // open: gt, lt
  Multiplexer #(.enable("false")) multiplexer_69 (.in0(1'b0), .in1(comparator_46_eq), .out(sb_t), .sel(MemRW));
  Multiplexer #(.enable("false")) multiplexer_70 (.in0(1'b0), .in1(comparator_47_eq), .out(sh), .sel(MemRW));
  Multiplexer #(.enable("false")) multiplexer_71 (.in0(1'b0), .in1(comparator_48_eq), .out(sw), .sel(MemRW));
  Comparator #(.width(3)) comparator_49 (.a(3'b000), .b(SBfunc3), .eq(comparator_49_eq));  // open: gt, lt
  Comparator #(.width(3)) comparator_50 (.a(3'b001), .b(SBfunc3), .eq(comparator_50_eq));  // open: gt, lt
  Comparator #(.width(3)) comparator_51 (.a(3'b100), .b(SBfunc3), .eq(comparator_51_eq));  // open: gt, lt
  Comparator #(.width(3)) comparator_52 (.a(3'b101), .b(SBfunc3), .eq(comparator_52_eq));  // open: gt, lt
  Comparator #(.width(3)) comparator_53 (.a(3'b110), .b(SBfunc3), .eq(comparator_53_eq));  // open: gt, lt
  Comparator #(.width(3)) comparator_54 (.a(3'b111), .b(SBfunc3), .eq(comparator_54_eq));  // open: gt, lt
  Multiplexer #(.enable("false")) multiplexer_72 (.in0(1'b0), .in1(comparator_49_eq), .out(beq), .sel(SB));
  Multiplexer #(.enable("false")) multiplexer_73 (.in0(1'b0), .in1(comparator_50_eq), .out(bne), .sel(SB));
  Multiplexer #(.enable("false")) multiplexer_74 (.in0(1'b0), .in1(comparator_51_eq), .out(blt), .sel(SB));
  Multiplexer #(.enable("false")) multiplexer_75 (.in0(1'b0), .in1(comparator_53_eq), .out(bltu), .sel(SB));
  Multiplexer #(.enable("false")) multiplexer_76 (.in0(1'b0), .in1(comparator_54_eq), .out(bgeu), .sel(SB));
  Multiplexer #(.enable("false")) multiplexer_77 (.in0(1'b0), .in1(comparator_52_eq), .out(bge), .sel(SB));

  // Other names for the same wires on the sheet: U_17 = auipc; csrwi = CSRSel; Iimm[11:0] = inst[31:20];
  //   Ifunc7[6:0] = inst[31:25]; UJ = jal; U_37 = lui; S = MemRW

  // Notes on the sheet:
  //   INPUTS to your circuit
  //   DON'T CHANGE THE LOCATIONS OF THE INPUTS AND OUTPUTS!
  //   OUTPUT from your circuit
  //   PCSel  BrUn(double check) CSRSel
  //   R Type
  //   I Type
  //   SB Type
  //   S Type
  //   U Type
  //   UJ Type
endmodule
