// Logisim project cpu.circ as structural Verilog: 1 circuit, main circuit cpu
module cpu (
  input  clk,
  input  [31:0] INSTRUCTION,
  input  [31:0] READ_DATA,
  output [31:0] WRITE_ADDRESS,
  output [31:0] PROGRAM_COUNTER,
  output [31:0] ra,
  output [31:0] sp,
  output [31:0] t0,
  output [31:0] t1,
  output [31:0] t2,
  output [31:0] s0,
  output [31:0] s1,
  output [31:0] a0,
  output [31:0] tohost,
  output [3:0] WRITE_ENABLE,
  output [31:0] WRITE_DATA
);

  wire ASel, BrEq, BrLt, BrUn, BSel, CSRSel, CSRWen, I_03, I_13, I_67, I_73, MemRW, nor_1_out, or_1_out,
       or_2_out, or_3_out, PCSel, R, RegWEn, S, SB, U_17, U_37, UJ;
  wire [1:0] WBSel;
  wire [2:0] control_logic_1_immsel;
  wire [3:0] control_logic_1_alusel;
  wire [4:0] rd, rs1, rs2;
  wire [31:0] adder_1_out, bit_extender_1_out, csr_data, imm, inst, multiplexer_1_out, multiplexer_2_out,
       multiplexer_5_out, multiplexer_6_out, PC_out, rd1, wd;

  Adder #(.width(32)) adder_1 (.a(PROGRAM_COUNTER), .b(32'h4), .out(adder_1_out));  // open: cin, cout
  Register #(.width(32)) PC (.D(multiplexer_1_out), .clk(clk), .Q(PROGRAM_COUNTER));  // open: en, clr
  Multiplexer #(.enable("false"), .width(32)) multiplexer_1 (
    .in0(adder_1_out), .in1(WRITE_ADDRESS), .out(multiplexer_1_out), .sel(PCSel));
  Register #(.width(32)) register_1 (.D(multiplexer_2_out), .clk(clk), .Q(inst));  // open: en, clr
  Multiplexer #(.enable("false"), .width(32)) multiplexer_2 (
    .in0(INSTRUCTION), .in1(32'h13), .out(multiplexer_2_out), .sel(PCSel));
  Comparator #(.width(7)) comparator_1 (.a(7'b0110011), .b(inst[6:0]), .eq(R));  // open: gt, lt
  Comparator #(.width(7)) comparator_2 (.a(7'b0000011), .b(inst[6:0]), .eq(I_03));  // open: gt, lt
  Comparator #(.width(7)) comparator_3 (.a(7'b0010011), .b(inst[6:0]), .eq(I_13));  // open: gt, lt
  Comparator #(.width(7)) comparator_4 (.a(7'b0100011), .b(inst[6:0]), .eq(S));  // open: gt, lt
  Comparator #(.width(7)) comparator_5 (.a(7'b1100011), .b(inst[6:0]), .eq(SB));  // open: gt, lt
  Comparator #(.width(7)) comparator_6 (.a(7'b0010111), .b(inst[6:0]), .eq(U_17));  // open: gt, lt
  Comparator #(.width(7)) comparator_7 (.a(7'b0110111), .b(inst[6:0]), .eq(U_37));  // open: gt, lt
  Comparator #(.width(7)) comparator_8 (.a(7'b1101111), .b(inst[6:0]), .eq(UJ));  // open: gt, lt
  Comparator #(.width(7)) comparator_9 (.a(7'b1100111), .b(inst[6:0]), .eq(I_67));  // open: gt, lt
  Comparator #(.width(7)) comparator_10 (.a(7'b1110011), .b(inst[6:0]), .eq(I_73));  // open: gt, lt
  // Probe on PCSel
  // Probe on RegWEn
  control_logic control_logic_1 (
    .CSRWen(CSRWen), .PCSel(PCSel), .RegWEn(RegWEn), .ImmSel(control_logic_1_immsel), .BrUn(BrUn),
    .ASel(ASel), .BSel(BSel), .ALUSel(control_logic_1_alusel), .MemRW(MemRW), .WBSel(WBSel), .CSRSel(CSRSel),
    .inst(inst), .BrEq(BrEq), .BrLt(BrLt));
  Register #(.width(32)) register_2 (.D(PROGRAM_COUNTER), .clk(clk), .Q(PC_out));  // open: en, clr
  imm_gen imm_gen_1 (.inst(inst), .ImmSel(control_logic_1_immsel), .imm(imm));
  // Probe on control_logic_1_immsel
  // Probe on BrEq
  // Probe on BrLt
  // Probe on BrUn
  // Probe on ASel
  // Probe on BSel
  // Probe on control_logic_1_alusel
  // Probe on MemRW
  Multiplexer #(.enable("false"), .width(5)) multiplexer_3 (
    .in0({5{1'b0}}), .in1(inst[11:7]), .out(rd), .sel(nor_1_out));
  nor nor_1 (nor_1_out, S, SB);
  regfile regfile_1 (
    .rs1(rs1), .rs2(rs2), .rd(rd), .Write_Data(wd), .RegWEn(1'b1), .clk(clk), .ra(ra), .sp(sp), .t0(t0),
    .t1(t1), .t2(t2), .s0(s0), .s1(s1), .a0(a0), .Read_Data_1(rd1), .Read_Data_2(WRITE_DATA));
  branch_comp branch_comp_1 (.rs1(rd1), .rs2(WRITE_DATA), .BrUn(BrUn), .BrEq(BrEq), .BrLt(BrLt));
  // Probe on WBSel
  // Probe on CSRSel
  Multiplexer #(.enable("false"), .width(5)) multiplexer_4 (
    .in0({5{1'b0}}), .in1(inst[24:20]), .out(rs2), .sel(or_1_out));
  or or_1 (or_1_out, R, S, SB);
  // Probe on ASel
  // Probe on BSel
  // Probe on CSRWen
  Multiplexer #(.enable("false"), .width(32)) multiplexer_5 (
    .in0(PC_out), .in1(rd1), .out(multiplexer_5_out), .sel(ASel));
  Multiplexer #(.enable("false"), .width(32)) multiplexer_6 (
    .in0(WRITE_DATA), .in1(imm), .out(multiplexer_6_out), .sel(BSel));
  assign bit_extender_1_out = {{27{rs1[4]}}, rs1};  // Bit_Extender bit_extender_1
  Multiplexer #(.enable("false"), .width(5)) multiplexer_7 (
    .in0({5{1'b0}}), .in1(inst[19:15]), .out(rs1), .sel(or_2_out));
  or or_2 (or_2_out, R, S, SB, or_3_out);
  Multiplexer #(.enable("false"), .width(32)) multiplexer_8 (
    .in0(rd1), .in1(bit_extender_1_out), .out(csr_data), .sel(CSRSel));
  or or_3 (or_3_out, I_03, I_13, I_67, I_73);
  // Probe on control_logic_1_alusel
  alu alu_1 (.Result(WRITE_ADDRESS), .A(multiplexer_5_out), .B(multiplexer_6_out), .ALUSel(control_logic_1_alusel));
  csr csr_1 (.CSR_address(inst[31:20]), .CSR_din(csr_data), .CSR_WE(CSRWen), .clk(clk), .tohost(tohost));
  Multiplexer #(.enable("false"), .select(2), .width(32)) multiplexer_9 (
    .in0({32{1'b0}}), .in1(WRITE_ADDRESS), .in2(READ_DATA), .in3(PC_out), .out(wd), .sel(WBSel));
  // Probe on WBSel
  assign WRITE_ENABLE = {{3{MemRW}}, MemRW};  // Bit_Extender bit_extender_2

  // Other names for the same wires on the sheet: rd2[31:0] = WRITE_DATA; Result[31:0] = WRITE_ADDRESS

  // Notes on the sheet:
  //   Output to IMEM
  //   IMEM (do **NOT** move this)
  //   Inputs from IMEM
  //   It is OK to move the PC, RegFile, ALU, MEM, Branch Comp, Imm Gen, and Control Logic to wherever is most convenient for you when constructing your CPU, and to delete this text
  //   Inputs/Outputs for testing. Do **NOT** move these.
  //   Outputs To DMEM
  //   DMEM (do **NOT** move this)
  //   Inputs From DMEM
endmodule
