// Logisim project regfile.circ as structural Verilog: 1 circuit, main circuit regfile
module regfile (
  input  [4:0] rs1,
  input  [4:0] rs2,
  input  [4:0] rd,
  input  [31:0] Write_Data,
  input  RegWEn,
  input  clk,
  output [31:0] ra,
  output [31:0] sp,
  output [31:0] t0,
  output [31:0] t1,
  output [31:0] t2,
  output [31:0] s0,
  output [31:0] s1,
  output [31:0] a0,
  output [31:0] Read_Data_1,
  output [31:0] Read_Data_2
);

  wire wA0, wRa, wS0, wS1, wSp, wT0, wT1, wT2;
  wire [4:0] and_1_out, bit_extender_1_out;
  wire [31:0] multiplexer_1_out, multiplexer_2_out, multiplexer_3_out, multiplexer_4_out, multiplexer_5_out,
       multiplexer_6_out, multiplexer_8_out, multiplexer_9_out;

  Register #(.width(32)) register_1 (.D(multiplexer_1_out), .clk(clk), .Q(t0));  // open: en, clr
  Multiplexer #(.enable("false"), .width(32)) multiplexer_1 (
    .in0(t0), .in1(Write_Data), .out(multiplexer_1_out), .sel(wT0));
  Register #(.width(32)) register_2 (.D(multiplexer_2_out), .clk(clk), .Q(s1));  // open: en, clr
  Multiplexer #(.enable("false"), .width(32)) multiplexer_2 (
    .in0(s1), .in1(Write_Data), .out(multiplexer_2_out), .sel(wS1));
  assign bit_extender_1_out = {{4{RegWEn}}, RegWEn};  // Bit_Extender bit_extender_1
  Register #(.width(32)) register_3 (.D(multiplexer_3_out), .clk(clk), .Q(ra));  // open: en, clr
  Multiplexer #(.enable("false"), .width(32)) multiplexer_3 (
    .in0(ra), .in1(Write_Data), .out(multiplexer_3_out), .sel(wRa));
  Multiplexer #(.enable("false"), .width(32)) multiplexer_4 (
    .in0(t2), .in1(Write_Data), .out(multiplexer_4_out), .sel(wT2));
  Register #(.width(32)) register_4 (.D(multiplexer_4_out), .clk(clk), .Q(t2));  // open: en, clr
  assign and_1_out = bit_extender_1_out & rd;  // AND_Gate and_1, 5 bits wide
  Demultiplexer #(.enable("false"), .select(5)) demultiplexer_1 (
    .out1(wRa), .out2(wSp), .out5(wT0), .out6(wT1), .out7(wT2), .out8(wS0), .out9(wS1), .out10(wA0),
    .in(RegWEn), .sel(and_1_out));  // open: out0, out3, out4, out11, out12, out13, out14, out15, out16, out17, out18, out19, out20, out21, out22, out23, out24, out25, out26, out27, out28, out29, out30, out31
  Register #(.width(32)) register_5 (.D(multiplexer_5_out), .clk(clk), .Q(sp));  // open: en, clr
  Multiplexer #(.enable("false"), .width(32)) multiplexer_5 (
    .in0(sp), .in1(Write_Data), .out(multiplexer_5_out), .sel(wSp));
  Register #(.width(32)) register_6 (.D(multiplexer_6_out), .clk(clk), .Q(s0));  // open: en, clr
  Multiplexer #(.enable("false"), .width(32)) multiplexer_6 (
    .in0(s0), .in1(Write_Data), .out(multiplexer_6_out), .sel(wS0));
  Multiplexer #(.enable("false"), .select(5), .width(32)) multiplexer_7 (
    .in0({32{1'b0}}), .in1(ra), .in2(sp), .in5(t0), .in6(t1), .in7(t2), .in8(s0), .in9(s1), .in10(a0),
    .out(Read_Data_1), .sel(rs1));  // open: in3, in4, in11, in12, in13, in14, in15, in16, in17, in18, in19, in20, in21, in22, in23, in24, in25, in26, in27, in28, in29, in30, in31
  Register #(.width(32)) register_7 (.D(multiplexer_8_out), .clk(clk), .Q(t1));  // open: en, clr
  Multiplexer #(.enable("false"), .width(32)) multiplexer_8 (
    .in0(t1), .in1(Write_Data), .out(multiplexer_8_out), .sel(wT1));
  Register #(.width(32)) register_8 (.D(multiplexer_9_out), .clk(clk), .Q(a0));  // open: en, clr
  Multiplexer #(.enable("false"), .width(32)) multiplexer_9 (
    .in0(a0), .in1(Write_Data), .out(multiplexer_9_out), .sel(wA0));
  Multiplexer #(.enable("false"), .select(5), .width(32)) multiplexer_10 (
    .in0({32{1'b0}}), .in1(ra), .in2(sp), .in5(t0), .in6(t1), .in7(t2), .in8(s0), .in9(s1), .in10(a0),
    .out(Read_Data_2), .sel(rs2));  // open: in3, in4, in11, in12, in13, in14, in15, in16, in17, in18, in19, in20, in21, in22, in23, in24, in25, in26, in27, in28, in29, in30, in31

  // Other names for the same wires on the sheet: read_data1[31:0] = Read_Data_1; read_data2[31:0] = Read_Data_2;
  //   read_reg1[4:0] = rs1; read_reg2[4:0] = rs2; write_en = RegWEn; write_reg[4:0] = rd

  // Notes on the sheet:
  //   INPUTS to your circuit
  //   DON'T CHANGE THE LOCATIONS OF THE INPUTS AND OUTPUTS!
  //   These are DEBUG/TEST outputs from your circuit.
  //   OUTPUTS from your circuit
endmodule
